# Fritzing sketch nielsen (saved by Fritzing 0.9.0b)
breadboards: 1

parts:
  U1 = atmega328 [package=dip]
  ICSP = AVR ISP 6 Pin [package=2x3_lock]
  LEDS = Header 5 [package=1x05-1mm-ra]
  R1 = Resistor [tolerance=±5% resistance=1k package=THT]
  R2 = Resistor [tolerance=±5% resistance=1k package=THT]
  R3 = Resistor [tolerance=±5% resistance=1k package=THT]
  R4 = Resistor [tolerance=±5% resistance=1k package=THT]
  KEY3 = Header 10 [package=1x10-2mm-smd]
  KEY2 = Header 10 [package=1x10-2mm-smd]
  KEY1 = Header 10 [package=1x10-2mm-smd]
  VOL = Header 2 [package=jst-2-pth]
  18-22pf = Capacitor [package=cap-pth-small2]
  18-22pf1 = Capacitor [package=cap-pth-small2]
  Y1 = CRYSTAL [package=crystal-smd-5x3]
  R5 = Resistor [tolerance=±5% resistance=220 package=THT]
  IC1 = L293D [package=THT]
  JP1 = Header 3 [package=screwterminal-3.5mm-3_lock.007s]
  VCC1 = Battery block 9V
  IC2 = Voltage Regulator [package=78xxl]
  C1 = Capacitor [package=cap-pth-small2]
  C2 = Electrolytic Capacitor [capacitance=100µF package="0405 [SMD, electrolytic]"]

nets:
  N1: U1.RESET, ICSP.5, R5.Pin_1
  N2: U1.D2, KEY3.1, KEY2.1, KEY1.1
  N3: U1.D3_(PWM), IC1.In_4
  N4: U1.D4, KEY3.2, KEY2.2, KEY1.2
  N5: U1.VCC, LEDS.5, IC1.Enable_1, IC1.Enable_2, IC1.+V, IC2.OUT, C1.1
  GND: U1.GND, ICSP.6, VOL.2, 18-22pf.2, R5.Pin_0, IC1.0V, VCC1.-, IC2.GND, C1.2, C2.-
  N6: U1.XLAT1, 18-22pf.1, Y1.1
  N7: U1.XLAT2, 18-22pf1.1, Y1.2
  N8: U1.D5_(PWM), IC1.In_3
  N9: U1.D6_(PWM), KEY3.3, KEY2.3, KEY1.3
  N10: U1.D7, KEY3.4, KEY2.4, KEY1.4
  N11: U1.D8, KEY3.5, KEY2.5, KEY1.5
  N12: U1.D9_(PWM), KEY3.6, KEY2.6, KEY1.6
  N13: U1.D10_(PWM), KEY3.7, KEY2.7, KEY1.7
  N14: U1.D11_(PWM), ICSP.4, IC1.In_2
  N15: U1.D12, ICSP.1, KEY3.8, KEY2.8, KEY1.8
  N16: U1.D13, ICSP.3, KEY3.9, KEY2.9, KEY1.9
  N17: U1.AVCC, ICSP.2
  N18: U1.A0, KEY3.10, KEY2.10, KEY1.10
  N19: U1.A1, VOL.1
  N20: U1.A2, R4.Pin_0
  N21: U1.A3, R3.Pin_0
  N22: U1.A4, R2.Pin_0
  N23: U1.A5, R1.Pin_0
  N24: LEDS.1, R1.Pin_1
  N25: LEDS.2, R2.Pin_1
  N26: LEDS.3, R3.Pin_1
  N27: LEDS.4, R4.Pin_1
  N28: IC1.Out_2_(_Controlled_by_Enable_1_), JP1.3
  N29: IC1.+Vmotor, VCC1.+, IC2.IN, C2.+
  N30: IC1.Out_3_(_Controlled_by_Enable_2_), JP1.2
  N31: IC1.Out_4_(_Controlled_by_Enable_2_), JP1.1
